// Logisim project ArrayFilter.circ as structural Verilog
module DataPath (
  input  wrJ,
  input  selMuxAddress,
  input  selMuxAdder,
  input  [7:0] data,
  input  selMuxReg,
  input  wrI,
  input  selMuxComp0,
  input  selMuxComp2,
  input  wrSize,
  input  selMuxComp1,
  input  rst,
  input  clk,
  input  [7:0] data_in,
  input  wrAux,
  output [7:0] address,
  output comp,
  output [7:0] data_out
);

  wire comparator_1_gt, comparator_1_lt;
  wire [7:0] adder_1_out, multiplexer_1_out, multiplexer_2_out, multiplexer_3_out, multiplexer_4_out,
       reg_I_q, reg_J_q, reg_size_q;

  // Probe on data
  Multiplexer #(.width(8), .enable("false")) multiplexer_1 (
    .in0(adder_1_out), .in1(data), .out(multiplexer_1_out), .sel(selMuxReg));
  Register reg_J (.D(multiplexer_1_out), .en(wrJ), .Q(reg_J_q), .clk(clk), .clr(rst));
  Register reg_I (.D(multiplexer_1_out), .en(wrI), .Q(reg_I_q), .clk(clk), .clr(rst));
  Register reg_size (.D(multiplexer_1_out), .en(wrSize), .Q(reg_size_q), .clk(clk), .clr(rst));
  Multiplexer #(.width(8), .enable("false")) multiplexer_2 (
    .in0(reg_J_q), .in1(reg_I_q), .out(multiplexer_2_out), .sel(selMuxAdder));
  Register reg_Aux (.D(data_in), .en(wrAux), .Q(data_out), .clk(clk), .clr(rst));
  Adder adder_1 (.a(multiplexer_2_out), .b(8'h1), .out(adder_1_out));  // open: cin, cout
  Multiplexer #(.width(8), .enable("false")) multiplexer_3 (
    .in0({8{1'b0}}), .in1(reg_I_q), .out(multiplexer_3_out), .sel(selMuxComp0));
  Multiplexer #(.width(8), .enable("false")) multiplexer_4 (
    .in0(reg_size_q), .in1(data_out), .out(multiplexer_4_out), .sel(selMuxComp1));
  Multiplexer #(.width(8), .enable("false")) multiplexer_5 (
    .in0(reg_J_q), .in1(reg_I_q), .out(address), .sel(selMuxAddress));
  Comparator comparator_1 (
    .a(multiplexer_3_out), .b(multiplexer_4_out), .gt(comparator_1_gt), .lt(comparator_1_lt));  // open: eq
  Multiplexer #(.enable("false")) multiplexer_6 (
    .in0(comparator_1_gt), .in1(comparator_1_lt), .out(comp), .sel(selMuxComp2));
endmodule
